# Fritzing sketch connections (saved by Fritzing 0.9.10b)

parts:
  OLED1 = OLED 128x64 I2C Monochrome Display GND-VDD
  RE1 = Rotary Encoder [package=THT]
  Part1 = Arduino Nano (Rev3.0) (ICSP)
  LED1 = LED - 5mm [color="Red (633nm)" current=0.030 package="5 mm [THT]"]
  LED2 = LED - 5mm [color="Red (633nm)" current=0.030 package="5 mm [THT]"]
  LED3 = LED - 5mm [color="Red (633nm)" current=0.030 package="5 mm [THT]"]
  LED4 = LED - 5mm [color="Red (633nm)" current=0.030 package="5 mm [THT]"]
  LED5 = LED - 5mm [color="Yellow (585nm)" current=0.030 package="5 mm [THT]"]
  LED6 = LED - 5mm [color="Yellow (595nm)" current=0.030 package="5 mm [THT]"]
  LED7 = LED - 5mm [color="Yellow (592nm)" current=0.030 package="5 mm [THT]"]
  LED8 = LED - 5mm [color="Yellow (595nm)" current=0.030 package="5 mm [THT]"]
  R1 = Resistor [tolerance=±5% power=0.25 resistance=220 package=THT]
  R2 = Resistor [tolerance=±5% power=0.25 resistance=220 package=THT]
  R3 = Resistor [tolerance=±5% power=0.25 resistance=220 package=THT]
  R4 = Resistor [tolerance=±5% power=0.25 resistance=220 package=THT]
  R5 = Resistor [tolerance=±5% power=0.25 resistance=220 package=THT]
  R6 = Resistor [tolerance=±5% power=0.25 resistance=220 package=THT]
  R7 = Resistor [tolerance=±5% power=0.25 resistance=220 package=THT]
  R8 = Resistor [tolerance=±5% power=0.25 resistance=220 package=THT]
  S1 = SWITCH-SPST-2 [package=switch-spst-vertical]
  BAT1 = Powerbank-DIY [package=battery-18650]
  M1 = Dagu DGServo 9g (Top view) [part_number=RS001B]

nets:
  GND: OLED1.GND, RE1.GND, RE1.SW-2, Part1.GND, LED1.cathode, LED2.cathode, LED3.cathode, LED4.cathode, LED5.cathode, LED6.cathode, LED7.cathode, LED8.cathode, BAT1.GND, M1.gnd
  VDD: OLED1.VDD, Part1.5V, S1.O, M1.vcc
  N1: OLED1.SCK, Part1.A4
  N2: OLED1.SDA, Part1.A5
  N3: RE1.Pin-A, Part1.D3
  N4: RE1.Pin-B, Part1.D4
  N5: RE1.SW-1, Part1.D2
  N6: Part1.D6, R7.Pin_1
  N7: Part1.D7, R4.Pin_1
  N8: Part1.D8, R5.Pin_1
  N9: Part1.D9, R3.Pin_1
  N10: Part1.D12/MISO, M1.pulse
  N11: Part1.A3, R1.Pin_1
  N12: Part1.A2, R8.Pin_1
  N13: Part1.A1, R2.Pin_1
  N14: Part1.A0, R6.Pin_1
  N15: LED1.anode, R8.Pin_0
  N16: LED2.anode, R5.Pin_0
  N17: LED3.anode, R6.Pin_0
  N18: LED4.anode, R7.Pin_0
  N19: LED5.anode, R4.Pin_0
  N20: LED6.anode, R2.Pin_0
  N21: LED7.anode, R3.Pin_0
  N22: LED8.anode, R1.Pin_0
  N23: S1.P, BAT1.5V

custom parts:
  OLED 128x64 I2C Monochrome Display GND-VDD: OLED 128x64 I2C Monochrome Display. Note: there are two variants of this part, this one is the GND VDD SCK SDA variant. The other is VDD GND SCK SDA. Make sure you select the part that matches your module as using the incorrect part will probably destroy your module! In addition the mounting holes are marked on silkscreen but not by default drilled. If you want drilled mounting holes, copy a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
  Rotary Encoder: Rotary Encoder with push button
  Powerbank-DIY: Powerbank-DIY (do it yourself) with one 18650 Li-ion battery cell and modded with dupont cables.
